# Fritzing sketch BlinkyLEDonButtonPress (saved by Fritzing 0.9.2b)
breadboards: 1

parts:
  R1 = Resistor [tolerance=±5% resistance=220 package=THT]
  LED1 = LED - 5mm [color="Red (633nm)" package="5 mm [THT]"]
  Raspberry_Pi2 = Raspberry Pi 2

nets:
  N1: R1.Pin_0, LED1.anode
  N2: R1.Pin_1, Raspberry_Pi2.3v3
  N3: LED1.cathode, Raspberry_Pi2.GPIO5

notes:
  LED
  Short - Cathode - Negative
  Long - Anode - Positive
  (pin nearest the flat edge of the casing is the cathode - negative)
